# Fritzing sketch brewflowmeter-breadborad (saved by Fritzing 0.9.1b)

parts:
  Composant1 = Arduino Uno (Rev3)
  5v/12v_Relay = Relay [part_number=FRS1B-S package=THT]
  LCD1 = LCD screen
  R1 = Trimmer Potentiometer [maximum_resistance=10kΩ package=THT]
  Rotary_Encoder = Rotary Encoder [package=THT]
  Solenoid_Valve = Solenoid

nets:
  N1: Composant1.D8, LCD1.DB6
  N2: Composant1.D9_PWM, LCD1.DB5
  N3: Composant1.D10_PWM/SS, LCD1.DB4
  N4: Composant1.D11_PWM/MOSI, LCD1.E
  N5: Composant1.D12/MISO, LCD1.RS
  N6: Composant1.GND, 5v/12v_Relay.COIL2, Rotary_Encoder.EncoderPinA
  N7: Composant1.D3_PWM, Rotary_Encoder.EncoderPinC
  N8: Composant1.D4, 5v/12v_Relay.COIL1
  N9: Composant1.D7, LCD1.DB7
  5V: Composant1.5V, LCD1.VDD, Rotary_Encoder.EncoderPinB
  N10: 5v/12v_Relay.C1, 5v/12v_Relay.C2, Solenoid_Valve.pin2
  N11: LCD1.V0, R1.wiper
